// Logisim project CRC.circ as structural Verilog: 2 circuits, main circuit CRC
module CRC (
  input  [7:0] A,
  input  [3:0] B,
  output [10:0] C
);

  wire [2:0] n4bit_mod2div_1_remainders, n4bit_mod2div_2_remainders, n4bit_mod2div_3_remainders,
       n4bit_mod2div_5_remainders, n4bit_mod2div_6_remainders, n4bit_mod2div_7_remainders;
  wire [3:1] n4bit_mod2div_4_remainders;

  _4bit_mod2div u_4bit_mod2div_1 (
    .dividend(A[7:4]), .divisor(B), .remainders(n4bit_mod2div_1_remainders));  // open: quotient
  _4bit_mod2div u_4bit_mod2div_2 (
    .dividend({n4bit_mod2div_1_remainders, A[3]}), .divisor(B), .remainders(n4bit_mod2div_2_remainders));  // open: quotient
  _4bit_mod2div u_4bit_mod2div_3 (
    .dividend({n4bit_mod2div_2_remainders, A[2]}), .divisor(B), .remainders(n4bit_mod2div_3_remainders));  // open: quotient
  _4bit_mod2div u_4bit_mod2div_4 (
    .dividend({n4bit_mod2div_3_remainders, A[1]}), .divisor(B), .remainders(n4bit_mod2div_4_remainders));  // open: quotient
  _4bit_mod2div u_4bit_mod2div_5 (
    .dividend({n4bit_mod2div_4_remainders, A[0]}), .divisor(B), .remainders(n4bit_mod2div_5_remainders));  // open: quotient
  _4bit_mod2div u_4bit_mod2div_6 (
    .dividend({n4bit_mod2div_5_remainders, 1'b0}), .divisor(B), .remainders(n4bit_mod2div_6_remainders));  // open: quotient
  _4bit_mod2div u_4bit_mod2div_7 (
    .dividend({n4bit_mod2div_6_remainders, 1'b0}), .divisor(B), .remainders(n4bit_mod2div_7_remainders));  // open: quotient
  _4bit_mod2div u_4bit_mod2div_8 (
    .dividend({n4bit_mod2div_7_remainders, 1'b0}), .divisor(B), .remainders(C[2:0]));  // open: quotient

  assign C[10:3] = A;

  // Other names for the same wires on the sheet: _6 = A[3]; _5 = A[2]; _4 = A[1]; _3 = A[0]; Remain[2:0] = C[2:0];
  //   _7 = A[4]; _8 = A[5]; _9 = A[6]; _10 = A[7]
endmodule

module _4bit_mod2div (
  input  [3:0] dividend,
  input  [3:0] divisor,
  output quotient,
  output [2:0] remainders
);

  wire [2:0] bit_extender_1_out, xor_1_out;

  xor xor_1 (xor_1_out[0], dividend[0], divisor[0]);
  xor xor_2 (xor_1_out[1], dividend[1], divisor[1]);
  xor xor_3 (xor_1_out[2], dividend[2], divisor[2]);
  // XOR_Gate xor_4 has open pins: in0=dividend[3], in1=divisor[3], out=open
  Bit_Extender #(.in_width(4), .out_width(3)) bit_extender_1 (.in(dividend), .out(bit_extender_1_out));
  Multiplexer #(.width(3)) multiplexer_1 (
    .in0(bit_extender_1_out), .in1(xor_1_out), .out(remainders), .sel(dividend[3]));  // open: en

  assign quotient = dividend[3];
endmodule
