// Logisim project grf.circ as structural Verilog: 1 circuit, main circuit grf
module grf (
  input  clk,
  input  reset,
  input  WE,
  input  [4:0] A1,
  input  [4:0] A2,
  input  [4:0] A3,
  input  [31:0] WD,
  output [31:0] RD1,
  output [31:0] RD2
);

  wire e0, e1, e2, e3, e4, e5, e6, e7, e8, e9, e10, e11, e12, e13, e14, e15, e16, e17, e18, e19, e20, e21,
       e22, e23, e24, e25, e26, e27, e28, e29, e30, e31;
  wire [31:0] I0, I1, I2, I3, I4, I5, I6, I7, I8, I9, I10, I11, I12, I13, I14, I15, I16, I17, I18, I19, I20,
       I21, I22, I23, I24, I25, I26, I27, I28, I29, I30, I31, O0, O1, O2, O3, O4, O5, O6, O7, O8, O9, O10,
       O11, O12, O13, O14, O15, O16, O17, O18, O19, O20, O21, O22, O23, O24, O25, O26, O27, O28, O29, O30,
       O31;

  Register #(.width(32)) register_1 (.D(I0), .en(e0), .Q(O0), .clk(clk), .clr(reset));
  Register #(.width(32)) register_2 (.D(I4), .en(e4), .Q(O4), .clk(clk), .clr(reset));
  Register #(.width(32)) register_3 (.D(I8), .en(e8), .Q(O8), .clk(clk), .clr(reset));
  Register #(.width(32)) register_4 (.D(I12), .en(e12), .Q(O12), .clk(clk), .clr(reset));
  Register #(.width(32)) register_5 (.D(I16), .en(e16), .Q(O16), .clk(clk), .clr(reset));
  Register #(.width(32)) register_6 (.D(I20), .en(e20), .Q(O20), .clk(clk), .clr(reset));
  Register #(.width(32)) register_7 (.D(I24), .en(e24), .Q(O24), .clk(clk), .clr(reset));
  Register #(.width(32)) register_8 (.D(I28), .en(e28), .Q(O28), .clk(clk), .clr(reset));
  Demultiplexer #(.select(5), .width(32)) demultiplexer_1 (
    .out0(I0), .out1(I1), .out2(I2), .out3(I3), .out4(I4), .out5(I5), .out6(I6), .out7(I7), .out8(I8),
    .out9(I9), .out10(I10), .out11(I11), .out12(I12), .out13(I13), .out14(I14), .out15(I15), .out16(I16),
    .out17(I17), .out18(I18), .out19(I19), .out20(I20), .out21(I21), .out22(I22), .out23(I23), .out24(I24),
    .out25(I25), .out26(I26), .out27(I27), .out28(I28), .out29(I29), .out30(I30), .out31(I31), .in(WD),
    .sel(A3));  // open: en
  Register #(.width(32)) register_9 (.D(I1), .en(e1), .Q(O1), .clk(clk), .clr(reset));
  Register #(.width(32)) register_10 (.D(I5), .en(e5), .Q(O5), .clk(clk), .clr(reset));
  Register #(.width(32)) register_11 (.D(I9), .en(e9), .Q(O9), .clk(clk), .clr(reset));
  Register #(.width(32)) register_12 (.D(I13), .en(e13), .Q(O13), .clk(clk), .clr(reset));
  Register #(.width(32)) register_13 (.D(I17), .en(e17), .Q(O17), .clk(clk), .clr(reset));
  Register #(.width(32)) register_14 (.D(I21), .en(e21), .Q(O21), .clk(clk), .clr(reset));
  Register #(.width(32)) register_15 (.D(I25), .en(e25), .Q(O25), .clk(clk), .clr(reset));
  Register #(.width(32)) register_16 (.D(I29), .en(e29), .Q(O29), .clk(clk), .clr(reset));
  Register #(.width(32)) register_17 (.D(I2), .en(e2), .Q(O2), .clk(clk), .clr(reset));
  Register #(.width(32)) register_18 (.D(I6), .en(e6), .Q(O6), .clk(clk), .clr(reset));
  Register #(.width(32)) register_19 (.D(I10), .en(e10), .Q(O10), .clk(clk), .clr(reset));
  Register #(.width(32)) register_20 (.D(I14), .en(e14), .Q(O14), .clk(clk), .clr(reset));
  Register #(.width(32)) register_21 (.D(I18), .en(e18), .Q(O18), .clk(clk), .clr(reset));
  Register #(.width(32)) register_22 (.D(I22), .en(e22), .Q(O22), .clk(clk), .clr(reset));
  Register #(.width(32)) register_23 (.D(I26), .en(e26), .Q(O26), .clk(clk), .clr(reset));
  Register #(.width(32)) register_24 (.D(I30), .en(e30), .Q(O30), .clk(clk), .clr(reset));
  Register #(.width(32)) register_25 (.D(I3), .en(e3), .Q(O3), .clk(clk), .clr(reset));
  Register #(.width(32)) register_26 (.D(I7), .en(e7), .Q(O7), .clk(clk), .clr(reset));
  Register #(.width(32)) register_27 (.D(I11), .en(e11), .Q(O11), .clk(clk), .clr(reset));
  Register #(.width(32)) register_28 (.D(I15), .en(e15), .Q(O15), .clk(clk), .clr(reset));
  Register #(.width(32)) register_29 (.D(I19), .en(e19), .Q(O19), .clk(clk), .clr(reset));
  Register #(.width(32)) register_30 (.D(I23), .en(e23), .Q(O23), .clk(clk), .clr(reset));
  Register #(.width(32)) register_31 (.D(I27), .en(e27), .Q(O27), .clk(clk), .clr(reset));
  Register #(.width(32)) register_32 (.D(I31), .en(e31), .Q(O31), .clk(clk), .clr(reset));
  Demultiplexer #(.select(5), .disabled(0)) demultiplexer_2 (
    .out0(e0), .out1(e1), .out2(e2), .out3(e3), .out4(e4), .out5(e5), .out6(e6), .out7(e7), .out8(e8),
    .out9(e9), .out10(e10), .out11(e11), .out12(e12), .out13(e13), .out14(e14), .out15(e15), .out16(e16),
    .out17(e17), .out18(e18), .out19(e19), .out20(e20), .out21(e21), .out22(e22), .out23(e23), .out24(e24),
    .out25(e25), .out26(e26), .out27(e27), .out28(e28), .out29(e29), .out30(e30), .out31(e31), .in(1'b1),
    .sel(A3), .en(WE));
  Multiplexer #(.select(5), .width(32)) multiplexer_1 (
    .in0({32{1'b0}}), .in1(O1), .in2(O2), .in3(O3), .in4(O4), .in5(O5), .in6(O6), .in7(O7), .in8(O8),
    .in9(O9), .in10(O10), .in11(O11), .in12(O12), .in13(O13), .in14(O14), .in15(O15), .in16(O16), .in17(O17),
    .in18(O18), .in19(O19), .in20(O20), .in21(O21), .in22(O22), .in23(O23), .in24(O24), .in25(O25),
    .in26(O26), .in27(O27), .in28(O28), .in29(O29), .in30(O30), .in31(O31), .out(RD1), .sel(A1));  // open: en
  Multiplexer #(.select(5), .width(32)) multiplexer_2 (
    .in0({32{1'b0}}), .in1(O1), .in2(O2), .in3(O3), .in4(O4), .in5(O5), .in6(O6), .in7(O7), .in8(O8),
    .in9(O9), .in10(O10), .in11(O11), .in12(O12), .in13(O13), .in14(O14), .in15(O15), .in16(O16), .in17(O17),
    .in18(O18), .in19(O19), .in20(O20), .in21(O21), .in22(O22), .in23(O23), .in24(O24), .in25(O25),
    .in26(O26), .in27(O27), .in28(O28), .in29(O29), .in30(O30), .in31(O31), .out(RD2), .sel(A2));  // open: en

  // Other names for the same wires on the sheet: enslt = WE
endmodule
