// Logisim project ftoi.circ as structural Verilog: 1 circuit, main circuit ftoi
module ftoi (
  input  [15:0] float,
  output [31:0] out_2
);

  wire and_1_out, comparator_1_eq, comparator_1_gt, comparator_2_eq, comparator_2_lt, comparator_3_gt,
       comparator_4_lt;
  wire [1:0] select;
  wire [4:0] move, subtractor_2_out, subtractor_3_out;
  wire [31:0] adder_1_out, bit_extender_1_out, bit_extender_2_out, multiplexer_1_out, multiplexer_2_out,
       Normal, not_1_out, shifter_1_out, shifter_2_out;

  // Probe on move
  Subtractor #(.width(5)) subtractor_1 (.a(float[14:10]), .b(5'b01111), .out(move));  // open: bin, bout
  Comparator #(.width(5), .mode("unsigned")) comparator_1 (
    .a(float[14:10]), .b({5{1'b0}}), .gt(comparator_1_gt), .eq(comparator_1_eq));  // open: lt
  Comparator #(.width(5), .mode("unsigned")) comparator_2 (
    .a(float[14:10]), .b({5{1'b1}}), .eq(comparator_2_eq), .lt(comparator_2_lt));  // open: gt
  and and_1 (and_1_out, comparator_1_gt, comparator_2_lt);
  // Probe on 5'b01010
  // Probe on 5'b01010
  Priority_Encoder #(.select(2)) priority_encoder_1 (
    .in0(comparator_1_eq), .in1(and_1_out), .in2(comparator_2_eq), .out(select));  // open: in3, gs, en_out, en_in
  assign bit_extender_1_out = {{21{1'b0}}, {1'b1, float[9:0]}};  // Bit_Extender bit_extender_1
  Subtractor #(.width(5)) subtractor_2 (.a(5'b01010), .b(move), .out(subtractor_2_out));  // open: bin, bout
  assign bit_extender_2_out = {{21{1'b0}}, {1'b1, float[9:0]}};  // Bit_Extender bit_extender_2
  Subtractor #(.width(5)) subtractor_3 (.a(move), .b(5'b01010), .out(subtractor_3_out));  // open: bin, bout
  Shifter #(.width(32), .shift("lr")) shifter_1 (
    .in(bit_extender_1_out), .\dist (subtractor_2_out), .out(shifter_1_out));
  Shifter #(.width(32)) shifter_2 (.in(bit_extender_2_out), .\dist (subtractor_3_out), .out(shifter_2_out));
  Multiplexer #(.width(32)) multiplexer_1 (
    .in0(shifter_1_out), .in1(shifter_2_out), .out(multiplexer_1_out), .sel(comparator_3_gt));  // open: en
  Comparator #(.width(5)) comparator_3 (.a(move), .b(5'b01010), .gt(comparator_3_gt));  // open: eq, lt
  // Probe on multiplexer_2_out
  // Probe on not_1_out
  Multiplexer #(.select(2), .width(32)) multiplexer_2 (
    .in0({32{1'b0}}), .in1(Normal), .in2({32{1'b0}}), .out(multiplexer_2_out), .sel(select));  // open: in3, en
  Comparator #(.width(5)) comparator_4 (.a(move), .b({5{1'b0}}), .lt(comparator_4_lt));  // open: gt, eq
  assign not_1_out = ~multiplexer_2_out;  // NOT_Gate not_1, 32 bits wide
  Multiplexer #(.width(32)) multiplexer_3 (
    .in0(multiplexer_1_out), .in1({32{1'b0}}), .out(Normal), .sel(comparator_4_lt));  // open: en
  Adder #(.width(32)) adder_1 (.a(not_1_out), .b(32'h1), .out(adder_1_out));  // open: cin, cout
  Multiplexer #(.width(32)) multiplexer_4 (
    .in0(multiplexer_2_out), .in1(adder_1_out), .out(out_2), .sel(float[15]));  // open: en

  // Other names for the same wires on the sheet: fractional_part[9:0] = float[9:0]; E[4:0] = float[14:10];
  //   flag = float[15]

  // Notes on the sheet:
  //   分类器
endmodule
