// Logisim project navigation.circ as structural Verilog: 4 circuits, main circuit navigation
module navigation (
  input  [1:0] dir,
  input  clk,
  input  reset,
  output arrive,
  output hit
);

  wire [2:0] \状态存储_1_state ;
  wire [3:0] \转态转移_1_out_3 ;

  // Probe on \转态转移_1_out_3 
  \转态转移  \u_转态转移_1  (.out_3(\转态转移_1_out_3 ), .state(\状态存储_1_state ), .dir(dir));
  \状态存储  \u_状态存储_1  (.in_1(\转态转移_1_out_3 ), .clk(clk), .reset(reset), .state(\状态存储_1_state ), .hit(hit));
  // Probe on \状态存储_1_state 
  \状态输出  \u_状态输出_1  (.state(\状态存储_1_state ), .arrive(arrive));
endmodule

// 状态转移
module \转态转移  (
  input  [2:0] state,
  input  [1:0] dir,
  output [3:0] out_3
);

  wire and_1_out, and_2_out, and_3_out, and_4_out, and_5_out, and_6_out, and_7_out, and_8_out, and_9_out,
       and_10_out, and_11_out, and_12_out, and_13_out, and_14_out, and_15_out, and_16_out, and_17_out,
       and_18_out, and_19_out, and_20_out, and_21_out, and_22_out, and_23_out, and_24_out, and_25_out,
       and_26_out, and_27_out, and_28_out, and_29_out, and_30_out, and_31_out, and_32_out, and_33_out,
       and_34_out, and_35_out, and_36_out, and_37_out, and_38_out, and_39_out, and_40_out, and_41_out,
       and_42_out, not_1_out, not_2_out, not_3_out, not_4_out, not_5_out, not_6_out, not_7_out, not_8_out,
       not_9_out, not_10_out, not_11_out, not_12_out, not_13_out, not_14_out, not_15_out, not_16_out,
       not_17_out, not_18_out, not_19_out, not_20_out, not_21_out, not_22_out, not_23_out, not_24_out,
       not_25_out, not_26_out, not_27_out, not_28_out, or_2_out, or_3_out, or_4_out, or_5_out, or_6_out,
       or_7_out, or_9_out, or_10_out;

  not not_1 (not_1_out, state[0]);
  not not_2 (not_2_out, dir[1]);
  not not_3 (not_3_out, dir[0]);
  not not_4 (not_4_out, dir[1]);
  not not_5 (not_5_out, state[1]);
  not not_6 (not_6_out, dir[1]);
  not not_7 (not_7_out, state[2]);
  not not_8 (not_8_out, state[1]);
  not not_9 (not_9_out, dir[1]);
  not not_10 (not_10_out, dir[0]);
  not not_11 (not_11_out, state[2]);
  not not_12 (not_12_out, state[0]);
  not not_13 (not_13_out, dir[1]);
  not not_14 (not_14_out, state[2]);
  not not_15 (not_15_out, state[1]);
  not not_16 (not_16_out, state[0]);
  and and_1 (and_1_out, state[1], not_1_out);
  and and_2 (and_2_out, and_1_out, and_3_out);
  and and_3 (and_3_out, not_2_out, not_3_out);
  and and_4 (and_4_out, state[1], state[0]);
  and and_5 (and_5_out, and_4_out, and_6_out);
  and and_6 (and_6_out, not_4_out, dir[0]);
  and and_7 (and_7_out, not_5_out, state[0]);
  and and_8 (and_8_out, and_7_out, not_17_out);
  not not_17 (not_17_out, dir[1]);
  and and_9 (and_9_out, state[0], not_6_out);
  and and_10 (and_10_out, and_9_out, not_18_out);
  not not_18 (not_18_out, dir[0]);
  and and_11 (and_11_out, state[1], not_19_out);
  not not_19 (not_19_out, state[0]);
  not not_20 (not_20_out, dir[1]);
  and and_12 (and_12_out, not_20_out, dir[0]);
  and and_13 (and_13_out, state[1], not_21_out);
  not not_21 (not_21_out, state[0]);
  and and_14 (and_14_out, dir[1], not_22_out);
  not not_22 (not_22_out, dir[0]);
  and and_15 (and_15_out, state[1], state[0]);
  and and_16 (and_16_out, dir[1], dir[0]);
  and and_17 (and_17_out, not_7_out, not_8_out);
  and and_18 (and_18_out, and_17_out, and_19_out);
  and and_19 (and_19_out, not_9_out, not_10_out);
  and and_20 (and_20_out, state[0], dir[1]);
  and and_21 (and_21_out, and_20_out, dir[0]);
  and and_22 (and_22_out, state[1], dir[1]);
  and and_23 (and_23_out, and_22_out, dir[0]);
  and and_24 (and_24_out, state[1], state[0]);
  and and_25 (and_25_out, and_24_out, not_23_out);
  not not_23 (not_23_out, dir[0]);
  and and_26 (and_26_out, not_11_out, not_12_out);
  and and_27 (and_27_out, and_26_out, and_28_out);
  and and_28 (and_28_out, not_13_out, dir[0]);
  and and_29 (and_29_out, not_14_out, not_15_out);
  and and_30 (and_30_out, and_29_out, and_31_out);
  and and_31 (and_31_out, not_16_out, dir[1]);
  not not_24 (not_24_out, state[2]);
  and and_32 (and_32_out, not_24_out, not_25_out);
  not not_25 (not_25_out, state[0]);
  and and_33 (and_33_out, dir[1], not_26_out);
  not not_26 (not_26_out, dir[0]);
  and and_34 (and_34_out, state[0], dir[1]);
  and and_35 (and_35_out, state[1], state[0]);
  not not_27 (not_27_out, dir[1]);
  and and_36 (and_36_out, not_27_out, not_28_out);
  not not_28 (not_28_out, dir[0]);
  or or_1 (out_3[3], and_2_out, and_5_out);
  or or_2 (or_2_out, and_8_out, and_10_out);
  and and_37 (and_37_out, and_11_out, and_12_out);
  and and_38 (and_38_out, and_13_out, and_14_out);
  and and_39 (and_39_out, and_15_out, and_16_out);
  or or_3 (or_3_out, and_18_out, and_21_out);
  or or_4 (or_4_out, and_23_out, and_25_out);
  or or_5 (or_5_out, and_27_out, and_30_out);
  and and_40 (and_40_out, and_32_out, and_33_out);
  and and_41 (and_41_out, and_34_out, dir[0]);
  and and_42 (and_42_out, and_35_out, and_36_out);
  or or_6 (or_6_out, or_2_out, and_37_out);
  or or_7 (or_7_out, and_38_out, and_39_out);
  or or_8 (out_3[1], or_3_out, or_4_out);
  or or_9 (or_9_out, or_5_out, and_40_out);
  or or_10 (or_10_out, and_41_out, and_42_out);
  or or_11 (out_3[2], or_6_out, or_7_out);
  or or_12 (out_3[0], or_9_out, or_10_out);
endmodule

module \状态存储  (
  input  [3:0] in_1,
  input  clk,
  input  reset,
  output [2:0] state,
  output hit
);

  Register #(.width(4)) register_1 (.D(in_1), .Q({state, hit}), .clk(clk), .clr(reset));  // open: en
endmodule

// 输出
module \状态输出  (
  input  [2:0] state,
  output arrive
);

  wire and_1_out, not_1_out, not_2_out;

  not not_1 (not_1_out, state[1]);
  and and_1 (and_1_out, state[2], not_1_out);
  not not_2 (not_2_out, state[0]);
  and and_2 (arrive, and_1_out, not_2_out);
endmodule
