// Logisim project fsm.circ as structural Verilog: 4 circuits, main circuit fsm
module fsm (
  input  clr,
  input  [1:0] In,
  output Z
);

  wire clock_1_out;
  wire [1:0] multiplexer_1_out, register_1_q, \状态转移_1_state_2 ;

  \状态转移  \u_状态转移_1  (.state(register_1_q), .In(In), .state_2(\状态转移_1_state_2 ));
  // Probe on multiplexer_1_out
  Multiplexer #(.width(2)) multiplexer_1 (
    .in0(\状态转移_1_state_2 ), .in1(2'b00), .out(multiplexer_1_out), .sel(clr));  // open: en
  // Probe on register_1_q
  Register #(.width(2)) register_1 (.D(multiplexer_1_out), .Q(register_1_q), .clk(clock_1_out));  // open: en, clr
  Clock clock_1 (.out(clock_1_out));
  \输出逻辑  \u_输出逻辑_1  (.state(register_1_q), .In(In), .out(Z));
endmodule

module \状态转移  (
  input  [1:0] state,
  input  [1:0] In,
  output [1:0] state_2
);

  wire and_1_out, and_2_out, and_3_out, and_4_out, and_5_out, and_6_out, and_7_out, not_1_out, not_2_out,
       not_3_out, not_4_out, not_5_out, not_6_out, not_7_out;

  not not_1 (not_1_out, state[1]);
  not not_2 (not_2_out, state[0]);
  not not_3 (not_3_out, state[0]);
  and and_1 (and_1_out, not_1_out, state[0]);
  not not_4 (not_4_out, In[0]);
  and and_2 (and_2_out, state[1], not_2_out);
  not not_5 (not_5_out, In[0]);
  not not_6 (not_6_out, In[1]);
  and and_3 (and_3_out, state[1], not_3_out);
  not not_7 (not_7_out, In[0]);
  and and_4 (and_4_out, and_1_out, not_4_out);
  and and_5 (and_5_out, and_2_out, not_5_out);
  and and_6 (and_6_out, not_6_out, In[0]);
  and and_7 (and_7_out, and_3_out, not_7_out);
  or or_1 (state_2[1], and_4_out, and_5_out);
  or or_2 (state_2[0], and_6_out, and_7_out);
endmodule

module \输出逻辑  (
  input  [1:0] state,
  input  [1:0] In,
  output out
);

  wire and_1_out, not_1_out, not_2_out;

  not not_1 (not_1_out, state[0]);
  and and_1 (and_1_out, state[1], not_1_out);
  not not_2 (not_2_out, In[0]);
  and and_2 (out, and_1_out, not_2_out);
endmodule

module test (
  input  [2:0] in_1,
  output out_2
);

  fsm fsm_1 (.clr(in_1[0]), .In(in_1[2:1]), .Z(out_2));
endmodule
