// Logisim project ALU.circ as structural Verilog: 1 circuit, main circuit ALU
module ALU (
  input  [2:0] in_1,
  input  [31:0] SrcA,
  input  [31:0] SrcB,
  input  [31:0] SrcA_2,
  input  [31:0] SrcB_2,
  output Zero,
  output [31:0] ALUResult,
  output [31:0] ALUResult_2
);

  wire comparator_1_lt;
  wire [31:0] adder_1_out, bit_extender_1_out, multiplexer_1_out, not_1_out, or_1_out;

  // Probe on SrcA
  // Probe on SrcB
  assign not_1_out = ~SrcB;  // NOT_Gate not_1, 32 bits wide
  Multiplexer #(.width(32)) multiplexer_1 (
    .in0(SrcB), .in1(not_1_out), .out(multiplexer_1_out), .sel(in_1[2]));  // open: en
  // Probe on ALUResult_2
  Subtractor #(.width(32)) subtractor_1 (.a(SrcA_2), .b(SrcB_2), .out(ALUResult_2));  // open: bin, bout
  assign or_1_out = SrcA | multiplexer_1_out;  // OR_Gate or_1, 32 bits wide
  Adder #(.width(32)) adder_1 (.a(SrcA), .b(multiplexer_1_out), .out(adder_1_out), .cin(in_1[2]));  // open: cout
  Comparator #(.width(32)) comparator_1 (.a(adder_1_out), .b({32{1'b0}}), .lt(comparator_1_lt));  // open: gt, eq
  assign bit_extender_1_out = {{31{1'b0}}, comparator_1_lt};  // Bit_Extender bit_extender_1
  Multiplexer #(.select(2), .width(32)) multiplexer_2 (
    .in1(or_1_out), .in2(adder_1_out), .in3(bit_extender_1_out), .out(ALUResult), .sel(in_1[1:0]));  // open: in0, en
  Comparator #(.width(32)) comparator_2 (.a(ALUResult), .b({32{1'b0}}), .eq(Zero));  // open: gt, lt
  // Probe on ALUResult

  // Other names for the same wires on the sheet: Operation[1:0] = in_1[1:0]; Bnegate = in_1[2]
endmodule
