// Logisim project 1的偶数次.circ as structural Verilog: 1 circuit, main circuit main
module main (
  input  [7:0] in_1,
  input  [2:0] in_2,
  output out_3,
  output [3:0] out_4
);

  wire bitselector_1_out;
  wire [3:0] bitadder_1_out;

  assign out_4 = {{1{1'b0}}, in_2};  // Bit_Extender bit_extender_1
  BitAdder bitadder_1 (.in0(in_1), .out(bitadder_1_out));
  BitSelector #(.width(4)) bitselector_1 (.in(bitadder_1_out), .out(bitselector_1_out), .sel(2'b00));
  Comparator #(.width(1)) comparator_1 (.a(bitselector_1_out), .b(1'b1), .eq(out_3));  // open: gt, lt
  BitFinder bitfinder_1 ();  // open: in, index, found
endmodule
