// Logisim project RAM ROM.circ as structural Verilog: 1 circuit, main circuit main
module main (
  input  [7:0] in_1,
  input  [7:0] in_2,
  input  [7:0] in_3,
  input  [7:0] in_4,
  input  in_5,
  input  in_6,
  input  in_7,
  input  in_8,
  input  in_9,
  input  in_10,
  output [7:0] out_11,
  output [7:0] out_12
);

  Random random_1 ();  // open: clk, next, out, clr
  D_Flip_Flop d_ff_1 ();  // open: clk, D, Q, Qn, preset, en, reset
  S_R_Flip_Flop s_r_ff_1 ();  // open: S, clk, R, Q, Qn, preset, reset, en
  Counter counter_1 ();  // open: load, D, count, Q, carry, clk, clr
  T_Flip_Flop t_ff_1 ();  // open: clk, T, Q, Qn, preset, reset, en
  Shift_Register shift_register_1 ();  // open: shift, in, clk, out, load, clr, d0, q0, d1, q1, d2, q2, d3, q3, d4, q4, d5, q5, d6, q6, d7, q7
  Register register_1 ();  // open: D, en, Q, clk, clr
  RAM #(.bus("separate")) ram_1 (
    .addr(in_1), .din(in_4), .data(out_11), .str(in_5), .sel(in_9), .clk(in_10), .ld(in_8), .clr(in_7));
  // _4bit_sort 4bit_sort_1: pin names not known
  ROM rom_1 (.addr(in_2), .data(out_12), .sel(in_6));

  // Notes on the sheet:
  //   contents of rom_1 (hex, n*v repeats v):
  //   0 32
endmodule
