// Logisim project Radix.circ as structural Verilog: 1 circuit, main circuit main
module main (
  input  [8:0] \input ,
  input  [1:0] op,
  output [3:0] _0ut1,
  output [3:0] _0ut2,
  output [3:0] _0ut3
);

  wire [3:0] hi8, hi10, hi16, low8, low10, mid8, mid10;
  wire [8:0] divider_1_out, divider_1_rem, divider_2_out, divider_2_rem, divider_3_out, divider_3_rem;

  assign hi16 = {{3{1'b0}}, \input [8]};  // Bit_Extender bit_extender_1
  assign low8 = {{1{1'b0}}, \input [2:0]};  // Bit_Extender bit_extender_2
  assign mid8 = {{1{1'b0}}, \input [5:3]};  // Bit_Extender bit_extender_3
  assign hi8 = {{1{1'b0}}, \input [8:6]};  // Bit_Extender bit_extender_4
  Divider #(.width(9)) divider_1 (.a(\input ), .b(9'ha), .out(divider_1_out), .rem(divider_1_rem));  // open: upper
  Bit_Extender #(.in_width(9), .out_width(4)) bit_extender_5 (.in(divider_1_rem), .out(low10));
  Divider #(.width(9)) divider_2 (
    .a(divider_1_out), .b(9'ha), .out(divider_2_out), .rem(divider_2_rem));  // open: upper
  Bit_Extender #(.in_width(9), .out_width(4)) bit_extender_6 (.in(divider_2_rem), .out(mid10));
  Multiplexer #(.select(2), .width(4)) multiplexer_1 (
    .in0(low8), .in1(low10), .in2(\input [3:0]), .out(_0ut1), .sel(op));  // open: in3, en
  Multiplexer #(.select(2), .width(4)) multiplexer_2 (
    .in0(mid8), .in1(mid10), .in2(\input [7:4]), .out(_0ut2), .sel(op));  // open: in3, en
  Multiplexer #(.select(2), .width(4)) multiplexer_3 (
    .in0(hi8), .in1(hi10), .in2(hi16), .out(_0ut3), .sel(op));  // open: in3, en
  Divider #(.width(9)) divider_3 (
    .a(divider_2_out), .b(9'ha), .out(divider_3_out), .rem(divider_3_rem));  // open: upper
  Bit_Extender #(.in_width(9), .out_width(4)) bit_extender_7 (.in(divider_3_rem), .out(hi10));

  // Other names for the same wires on the sheet: low16[3:0] = \input [3:0]; mid16[3:0] = \input [7:4]
endmodule
