// Logisim project Tunnel.circ as structural Verilog: 1 circuit, main circuit main
module main (
  input  [31:0] \input ,
  output [31:0] out_2
);


  assign out_2 = \input ;

  // Other names for the same wires on the sheet: sample[31:0] = \input 
endmodule
