// Logisim project Logisim_fibonacci.circ as structural Verilog: 4 circuits, main circuit output
module \output  (
  input  [3:0] Date,
  input  Enable,
  input  clk,
  input  Sel,
  output [3:0] \output 
);

  wire [3:0] register_1_q;

  Register #(.width(4)) register_1 (.D(Date), .en(Enable), .Q(register_1_q), .clk(clk));  // open: clr
  Multiplexer #(.width(4)) multiplexer_1 (.in0(4'b0000), .in1(register_1_q), .out(\output ), .sel(Sel));  // open: en
endmodule

module main (
  input  [2:0] in_1,
  output [3:0] out_2
);

  wire clk, comparator_1_gt, not_1_out;
  wire [3:0] \状态存储_1_o1 , \状态存储_1_o2 , \状态转移_1_out_3 ;
  wire [7:0] adder_1_out, bit_extender_1_out, counter_1_q;

  Clock clock_1 (.out(clk));
  \状态转移  \u_状态转移_1  (.in_1(\状态存储_1_o1 ), .in_2(\状态存储_1_o2 ), .out_3(\状态转移_1_out_3 ));
  Counter #(.max('h40)) counter_1 (.Q(counter_1_q), .clk(clk));  // open: load, D, count, carry, clr
  assign bit_extender_1_out = {{5{1'b0}}, in_1};  // Bit_Extender bit_extender_1
  \状态存储  \u_状态存储_1  (.in_1(\状态转移_1_out_3 ), .in_2(clk), .o1(\状态存储_1_o1 ), .o2(\状态存储_1_o2 ));
  Adder adder_1 (.a(bit_extender_1_out), .b(8'h1), .out(adder_1_out));  // open: cin, cout
  not not_1 (not_1_out, comparator_1_gt);
  Comparator #(.mode("unsigned")) comparator_1 (
    .a(counter_1_q), .b(adder_1_out), .gt(comparator_1_gt));  // open: eq, lt
  \output  output_1 (.Date(\状态存储_1_o2 ), .Enable(not_1_out), .clk(clk), .Sel(comparator_1_gt), .\output (out_2));

  // Other names for the same wires on the sheet: input[2:0] = in_1
endmodule

module \状态转移  (
  input  [3:0] in_1,
  input  [3:0] in_2,
  output [3:0] out_3
);

  Adder #(.width(4)) adder_1 (.a(in_1), .b(in_2), .out(out_3));  // open: cin, cout
endmodule

module \状态存储  (
  input  [3:0] in_1,
  input  in_2,
  output [3:0] o1,
  output [3:0] o2
);

  wire comparator_1_eq;
  wire [3:0] register_1_q, register_2_q;
  wire [7:0] counter_1_q;

  Register #(.width(4)) register_1 (.D(in_1), .Q(register_1_q), .clk(in_2));  // open: en, clr
  Counter counter_1 (.Q(counter_1_q), .clk(in_2));  // open: load, D, count, carry, clr
  Register #(.width(4)) register_2 (.D(register_1_q), .Q(register_2_q), .clk(in_2));  // open: en, clr
  Comparator #(.mode("unsigned")) comparator_1 (.a({8{1'b0}}), .b(counter_1_q), .eq(comparator_1_eq));  // open: gt, lt
  Multiplexer #(.width(4)) multiplexer_1 (
    .in0(register_1_q), .in1(4'b0001), .out(o1), .sel(comparator_1_eq));  // open: en
  Multiplexer #(.width(4)) multiplexer_2 (
    .in0(register_2_q), .in1(4'b0000), .out(o2), .sel(comparator_1_eq));  // open: en
endmodule
