// Logisim project Logisim_fibonacci2.circ as structural Verilog: 3 circuits, main circuit Reg
module Reg (
  input  [31:0] A,
  input  [31:0] B,
  input  [31:0] C,
  input  [31:0] D,
  input  Enable_freeze,
  output [31:0] O5,
  output [31:0] O1,
  output [31:0] O6,
  output [31:0] O2,
  output [31:0] O4,
  output [31:0] O3
);

  wire clk;

  Clock clock_1 (.out(clk));
  Register #(.width(32)) register_1 (.D(A), .en(Enable_freeze), .Q(O1), .clk(clk));  // open: clr
  Register #(.width(32)) register_2 (.D(C), .en(Enable_freeze), .Q(O3), .clk(clk));  // open: clr
  Register #(.width(32)) register_3 (.D(B), .en(Enable_freeze), .Q(O2), .clk(clk));  // open: clr
  Register #(.width(32)) register_4 (.D(D), .en(Enable_freeze), .Q(O4), .clk(clk));  // open: clr

  assign O5 = A;
  assign O6 = B;
endmodule

module main (
  input  [31:0] Input,
  output [31:0] Output
);

  wire clock_1_out, comparator_1_gt, comparator_1_lt, comparator_2_gt, comparator_3_gt, comparator_4_gt;
  wire [31:0] adder_1_out, counter_1_q, mul_martrix_1_o5, mul_martrix_1_o6, multiplexer_1_out,
       multiplexer_3_out, subtractor_1_out;

  Clock clock_1 (.out(clock_1_out));
  Subtractor #(.width(32)) subtractor_1 (.a(Input), .b(32'h1), .out(subtractor_1_out));  // open: bin, bout
  Counter #(.width(32), .max('hffffffff)) counter_1 (
    .Q(counter_1_q), .clk(clock_1_out));  // open: load, D, count, carry, clr
  Comparator #(.width(32), .mode("unsigned")) comparator_1 (
    .a(subtractor_1_out), .b(counter_1_q), .gt(comparator_1_gt), .lt(comparator_1_lt));  // open: eq
  Comparator #(.width(32), .mode("unsigned")) comparator_2 (
    .a(counter_1_q), .b(32'h1), .gt(comparator_2_gt));  // open: eq, lt
  Comparator #(.width(32), .mode("unsigned")) comparator_3 (
    .a(Input), .b({32{1'b0}}), .gt(comparator_3_gt));  // open: eq, lt
  Comparator #(.width(32), .mode("unsigned")) comparator_4 (
    .a(Input), .b(32'h2), .gt(comparator_4_gt));  // open: eq, lt
  mul_martrix mul_martrix_1 (
    .Enable(comparator_1_gt), .Sel(comparator_2_gt), .O5(mul_martrix_1_o5), .O6(mul_martrix_1_o6));  // open: O1, O2, O3, O4
  Adder #(.width(32)) adder_1 (.a(mul_martrix_1_o5), .b(mul_martrix_1_o6), .out(adder_1_out));  // open: cin, cout
  Multiplexer #(.width(32)) multiplexer_1 (
    .in0({32{1'b0}}), .in1(32'h1), .out(multiplexer_1_out), .sel(comparator_3_gt));  // open: en
  Multiplexer #(.width(32)) multiplexer_2 (
    .in0(multiplexer_1_out), .in1(multiplexer_3_out), .out(Output), .sel(comparator_4_gt));  // open: en
  Multiplexer #(.width(32)) multiplexer_3 (
    .in0({32{1'b0}}), .in1(adder_1_out), .out(multiplexer_3_out), .sel(comparator_1_lt));  // open: en
endmodule

module mul_martrix (
  input  Enable,
  input  Sel,
  output [31:0] O1,
  output [31:0] O2,
  output [31:0] O3,
  output [31:0] O5,
  output [31:0] O4,
  output [31:0] O6
);

  wire [31:0] A, C, multiplexer_1_out, multiplexer_2_out, multiplexer_3_out, multiplexer_4_out;

  Multiplexer #(.width(32)) multiplexer_1 (.in0(32'h1), .in1(A), .out(multiplexer_1_out), .sel(Sel));  // open: en
  Multiplexer #(.width(32)) multiplexer_2 (.in0(32'h1), .in1(O1), .out(multiplexer_2_out), .sel(Sel));  // open: en
  Multiplexer #(.width(32)) multiplexer_3 (.in0(32'h1), .in1(C), .out(multiplexer_3_out), .sel(Sel));  // open: en
  Multiplexer #(.width(32)) multiplexer_4 (.in0({32{1'b0}}), .in1(O3), .out(multiplexer_4_out), .sel(Sel));  // open: en
  Reg reg_1 (
    .A(multiplexer_1_out), .C(multiplexer_3_out), .D(multiplexer_4_out), .Enable_freeze(Enable), .O1(O1),
    .O2(O2), .O4(O4), .O3(O3), .B(multiplexer_2_out), .O5(O5), .O6(O6));
  Adder #(.width(32)) adder_1 (.a(O1), .b(O2), .out(A));  // open: cin, cout
  Adder #(.width(32)) adder_2 (.a(O3), .b(O4), .out(C));  // open: cin, cout
endmodule
