// Logisim project Logisim_fibonacci2_.circ as structural Verilog: 4 circuits, main circuit main
module Reg (
  input  [31:0] A,
  input  [31:0] B,
  input  [31:0] C,
  input  [31:0] D,
  input  Enable_freeze,
  output [31:0] O1,
  output [31:0] O2,
  output [31:0] O4,
  output [31:0] O3
);

  wire clk;

  Clock clock_1 (.out(clk));
  Register #(.width(32)) register_1 (.D(A), .en(Enable_freeze), .Q(O1), .clk(clk));  // open: clr
  Register #(.width(32)) register_2 (.D(C), .en(Enable_freeze), .Q(O3), .clk(clk));  // open: clr
  Register #(.width(32)) register_3 (.D(B), .en(Enable_freeze), .Q(O2), .clk(clk));  // open: clr
  Register #(.width(32)) register_4 (.D(D), .en(Enable_freeze), .Q(O4), .clk(clk));  // open: clr
endmodule

// 快速幂
module Mul_Martrix (
  input  Enable,
  input  Sel,
  output [31:0] O1,
  output [31:0] O2,
  output [31:0] O3,
  output [31:0] O4
);

  wire [31:0] A, B, C, D, multiplexer_1_out, multiplexer_2_out, multiplexer_3_out, multiplexer_4_out,
       multiplier_1_out, multiplier_2_out, multiplier_3_out, multiplier_4_out, multiplier_5_out,
       multiplier_6_out, multiplier_7_out, multiplier_8_out;

  Multiplexer #(.width(32)) multiplexer_1 (.in0(32'h1), .in1(A), .out(multiplexer_1_out), .sel(Sel));  // open: en
  Multiplexer #(.width(32)) multiplexer_2 (.in0(32'h1), .in1(B), .out(multiplexer_2_out), .sel(Sel));  // open: en
  Multiplexer #(.width(32)) multiplexer_3 (.in0(32'h1), .in1(C), .out(multiplexer_3_out), .sel(Sel));  // open: en
  Multiplexer #(.width(32)) multiplexer_4 (.in0({32{1'b0}}), .in1(D), .out(multiplexer_4_out), .sel(Sel));  // open: en
  // Probe on O1
  Reg reg_1 (
    .A(multiplexer_1_out), .C(multiplexer_3_out), .D(multiplexer_4_out), .Enable_freeze(Enable), .O1(O1),
    .O2(O2), .O4(O4), .O3(O3), .B(multiplexer_2_out));
  Multiplier #(.width(32)) multiplier_1 (.a(O1), .b(O1), .out(multiplier_1_out));  // open: cin, cout
  Multiplier #(.width(32)) multiplier_2 (.a(O2), .b(O3), .out(multiplier_2_out));  // open: cin, cout
  Multiplier #(.width(32)) multiplier_3 (.a(O2), .b(O1), .out(multiplier_3_out));  // open: cin, cout
  Multiplier #(.width(32)) multiplier_4 (.a(O2), .b(O4), .out(multiplier_4_out));  // open: cin, cout
  Adder #(.width(32)) adder_1 (.a(multiplier_1_out), .b(multiplier_2_out), .out(A));  // open: cin, cout
  Adder #(.width(32)) adder_2 (.a(multiplier_3_out), .b(multiplier_4_out), .out(B));  // open: cin, cout
  Multiplier #(.width(32)) multiplier_5 (.a(O1), .b(O3), .out(multiplier_5_out));  // open: cin, cout
  Multiplier #(.width(32)) multiplier_6 (.a(O2), .b(O4), .out(multiplier_6_out));  // open: cin, cout
  Multiplier #(.width(32)) multiplier_7 (.a(O3), .b(O2), .out(multiplier_7_out));  // open: cin, cout
  Multiplier #(.width(32)) multiplier_8 (.a(O4), .b(O4), .out(multiplier_8_out));  // open: cin, cout
  Adder #(.width(32)) adder_3 (.a(multiplier_5_out), .b(multiplier_6_out), .out(C));  // open: cin, cout
  Adder #(.width(32)) adder_4 (.a(multiplier_7_out), .b(multiplier_8_out), .out(D));  // open: cin, cout
endmodule

module main (
  input  [31:0] in_1,
  output [31:0] out_2
);

  wire clk, comparator_1_gt, comparator_2_gt, comparator_3_gt, comparator_5_gt, Judge, register_3_q;
  wire [31:0] adder_1_out, and_1_out, counter_1_q, counter_2_q, counter_3_q, Input, mul_martrix_1_o1,
       mul_martrix_1_o2, mul_martrix_1_o3, mul_martrix_1_o4, mul_martrix_a_b_1_o1, mul_martrix_a_b_1_o2,
       register_1_q, register_2_q, Shift, Shift_input;

  Counter #(.width(32), .max('hffffffff)) counter_1 (.Q(counter_1_q), .clk(clk));  // open: load, D, count, carry, clr
  Clock clock_1 (.out(clk));
  Register #(.width(32)) register_1 (.D(Input), .Q(register_1_q), .clk(clk));  // open: en, clr
  Register #(.width(32)) register_2 (.D(Shift), .Q(register_2_q), .clk(clk));  // open: en, clr
  // Probe on Shift_input
  Multiplexer #(.width(32)) multiplexer_1 (
    .in0(register_1_q), .in1(register_2_q), .out(Shift_input), .sel(comparator_1_gt));  // open: en
  Comparator #(.width(32), .mode("unsigned")) comparator_1 (
    .a(counter_1_q), .b(32'h1), .gt(comparator_1_gt));  // open: eq, lt
  Subtractor #(.width(32)) subtractor_1 (.a(in_1), .b(32'h2), .out(Input));  // open: bin, bout
  // Probe on Shift
  Shifter #(.width(32), .shift("lr")) shifter_1 (.in(Shift_input), .\dist (5'b00001), .out(Shift));
  Counter #(.width(32), .max('hffffffff)) counter_2 (.Q(counter_2_q), .clk(clk));  // open: load, D, count, carry, clr
  Counter #(.width(32), .max('hffffffff)) counter_3 (.Q(counter_3_q), .clk(Judge));  // open: load, D, count, carry, clr
  Comparator #(.width(32), .mode("unsigned")) comparator_2 (
    .a(counter_2_q), .b({32{1'b0}}), .gt(comparator_2_gt));  // open: eq, lt
  Comparator #(.width(32)) comparator_3 (.a(counter_3_q), .b({32{1'b0}}), .gt(comparator_3_gt));  // open: eq, lt
  assign and_1_out = Shift_input & 32'h1;  // AND_Gate and_1, 32 bits wide
  // Probe on mul_martrix_1_o1
  Mul_Martrix mul_martrix_1 (
    .Enable(1'b1), .Sel(comparator_2_gt), .O1(mul_martrix_1_o1), .O2(mul_martrix_1_o2),
    .O3(mul_martrix_1_o3), .O4(mul_martrix_1_o4));
  Register #(.width(1)) register_3 (.D(comparator_3_gt), .Q(register_3_q), .clk(clk));  // open: en, clr
  Comparator #(.width(32), .mode("unsigned")) comparator_4 (.a(and_1_out), .b(32'h1), .eq(Judge));  // open: gt, lt
  // Probe on mul_martrix_a_b_1_o1
  Mul_Martrix_A_B mul_martrix_a_b_1 (
    .Enable(Judge), .Sel(register_3_q), .i1(mul_martrix_1_o1), .i2(mul_martrix_1_o2), .i3(mul_martrix_1_o3),
    .i4(mul_martrix_1_o4), .O1(mul_martrix_a_b_1_o1), .O2(mul_martrix_a_b_1_o2));  // open: O3, O4
  // Probe on mul_martrix_a_b_1_o2
  Adder #(.width(32)) adder_1 (
    .a(mul_martrix_a_b_1_o1), .b(mul_martrix_a_b_1_o2), .out(adder_1_out));  // open: cin, cout
  Multiplexer #(.width(32)) multiplexer_2 (
    .in0(adder_1_out), .in1({32{1'b0}}), .out(out_2), .sel(comparator_5_gt));  // open: en
  Comparator #(.width(32), .mode("unsigned")) comparator_5 (
    .a(Shift_input), .b({32{1'b0}}), .gt(comparator_5_gt));  // open: eq, lt
endmodule

// 矩阵乘法
module Mul_Martrix_A_B (
  input  Enable,
  input  Sel,
  input  [31:0] i1,
  input  [31:0] i2,
  input  [31:0] i3,
  input  [31:0] i4,
  output [31:0] O1,
  output [31:0] O2,
  output [31:0] O3,
  output [31:0] O4
);

  wire [31:0] A, adder_1_out, B, C, D, multiplexer_1_out, multiplexer_2_out, multiplexer_3_out,
       multiplexer_4_out, multiplier_1_out, multiplier_2_out, multiplier_3_out, multiplier_4_out,
       multiplier_5_out, multiplier_6_out, multiplier_7_out, multiplier_8_out;

  // Probe on i1
  // Probe on multiplexer_1_out
  Multiplexer #(.width(32)) multiplexer_1 (.in0(i1), .in1(A), .out(multiplexer_1_out), .sel(Sel));  // open: en
  Multiplexer #(.width(32)) multiplexer_2 (.in0(i2), .in1(B), .out(multiplexer_2_out), .sel(Sel));  // open: en
  Multiplexer #(.width(32)) multiplexer_3 (.in0(i3), .in1(C), .out(multiplexer_3_out), .sel(Sel));  // open: en
  Multiplexer #(.width(32)) multiplexer_4 (.in0(i4), .in1(D), .out(multiplexer_4_out), .sel(Sel));  // open: en
  Adder #(.width(32)) adder_1 (.a(multiplexer_1_out), .b(multiplexer_2_out), .out(adder_1_out));  // open: cin, cout
  Reg reg_1 (
    .A(multiplexer_1_out), .C(multiplexer_3_out), .D(multiplexer_4_out), .Enable_freeze(Enable), .O1(O1),
    .O2(O2), .O4(O4), .O3(O3), .B(multiplexer_2_out));
  // Probe on adder_1_out
  Multiplier #(.width(32)) multiplier_1 (.a(O1), .b(i1), .out(multiplier_1_out));  // open: cin, cout
  Multiplier #(.width(32)) multiplier_2 (.a(O2), .b(i3), .out(multiplier_2_out));  // open: cin, cout
  Multiplier #(.width(32)) multiplier_3 (.a(O1), .b(i2), .out(multiplier_3_out));  // open: cin, cout
  Multiplier #(.width(32)) multiplier_4 (.a(O2), .b(i4), .out(multiplier_4_out));  // open: cin, cout
  Adder #(.width(32)) adder_2 (.a(multiplier_1_out), .b(multiplier_2_out), .out(A));  // open: cin, cout
  // Probe on A
  Adder #(.width(32)) adder_3 (.a(multiplier_3_out), .b(multiplier_4_out), .out(B));  // open: cin, cout
  // Probe on B
  Multiplier #(.width(32)) multiplier_5 (.a(O3), .b(i1), .out(multiplier_5_out));  // open: cin, cout
  Multiplier #(.width(32)) multiplier_6 (.a(O4), .b(i3), .out(multiplier_6_out));  // open: cin, cout
  Multiplier #(.width(32)) multiplier_7 (.a(O3), .b(i2), .out(multiplier_7_out));  // open: cin, cout
  Multiplier #(.width(32)) multiplier_8 (.a(O4), .b(i4), .out(multiplier_8_out));  // open: cin, cout
  Adder #(.width(32)) adder_4 (.a(multiplier_5_out), .b(multiplier_6_out), .out(C));  // open: cin, cout
  Adder #(.width(32)) adder_5 (.a(multiplier_7_out), .b(multiplier_8_out), .out(D));  // open: cin, cout
endmodule
