// Logisim project keyboard and LED.circ as structural Verilog: 1 circuit, main circuit main
module main (
  input  in_1,
  input  in_2,
  input  in_3,
  input  in_4,
  input  [3:0] in_5,
  input  [31:0] in_6,
  input  in_7
);

  wire button_1_out, clock_1_out, nor_1_out;
  wire [6:0] keyboard_1_data;

  Clock clock_1 (.out(clock_1_out));
  Keyboard keyboard_1 (.clk(clock_1_out), .re(in_1), .clr(in_2), .data(keyboard_1_data));  // open: avail
  // NOR_Gate nor_1 has open pins: out=nor_1_out
  // OR_Gate or_1 is placed but not wired
  // XNOR_Gate xnor_1 is placed but not wired
  _7_Segment_Display u_7_segment_display_1 ();  // open: g, f, a, b, e, d, c, dp
  // XOR_Gate xor_1 has open pins: in1=nor_1_out, out=open
  TTY tty_1 (.data(keyboard_1_data), .clk(clock_1_out), .we(in_3), .clr(in_4));
  Hex_Digit_Display hex_digit_display_1 (.value(in_5), .dp(in_7));
  LED led_1 (.in(button_1_out));
  Button button_1 (.out(button_1_out));
  Joystick joystick_1 ();  // open: x, y
  DotMatrix #(.matrixcols(32), .matrixrows(32)) dotmatrix_1 (.col1(in_6));  // open: col0, col2, col3, col4, col5, col6, col7, col8, col9, col10, col11, col12, col13, col14, col15, col16, col17, col18, col19, col20, col21, col22, col23, col24, col25, col26, col27, col28, col29, col30, col31
endmodule
