// Logisim project Logisim_mod5.circ as structural Verilog: 3 circuits, main circuit mod5
module mod5 (
  input  in_1,
  output out_2,
  output out_3,
  output out_4,
  output out_5,
  output out_6
);

  wire reg_1_out_6, reg_1_out_7, reg_1_out_8, reg_1_out_9, reg_1_out_10;

  trans trans_1 (
    .\input (in_1), .i0(reg_1_out_6), .i1(reg_1_out_7), .i2(reg_1_out_8), .i3(reg_1_out_9),
    .i4(reg_1_out_10), .o0(out_2), .o1(out_3), .o2(out_4), .o3(out_5), .o4(out_6));
  \reg  reg_1 (
    .in_1(out_2), .in_2(out_3), .in_3(out_4), .in_4(out_5), .in_5(out_6), .out_6(reg_1_out_6),
    .out_7(reg_1_out_7), .out_8(reg_1_out_8), .out_9(reg_1_out_9), .out_10(reg_1_out_10));
endmodule

module trans (
  input  \input ,
  input  i0,
  input  i1,
  input  i2,
  input  i3,
  input  i4,
  output o0,
  output o1,
  output o2,
  output o3,
  output o4
);

  wire and_1_out, and_2_out, and_3_out, and_4_out, and_5_out, and_6_out, not_1_out, not_2_out, not_3_out,
       not_4_out, not_5_out, not_6_out, not_7_out;

  not not_1 (not_1_out, \input );
  not not_2 (not_2_out, i2);
  not not_3 (not_3_out, i2);
  and and_1 (and_1_out, \input , i3);
  and and_2 (and_2_out, \input , i2);
  not not_4 (not_4_out, \input );
  not not_5 (not_5_out, \input );
  and and_3 (and_3_out, not_1_out, not_2_out);
  not not_6 (not_6_out, i3);
  and and_4 (and_4_out, \input , not_3_out);
  not not_7 (not_7_out, i3);
  or or_1 (o3, and_1_out, and_2_out);
  and and_5 (and_5_out, not_4_out, i3);
  and and_6 (and_6_out, not_5_out, i2);
  and and_7 (o1, and_3_out, not_6_out);
  and and_8 (o2, and_4_out, not_7_out);
  or or_2 (o4, and_5_out, and_6_out);

  assign o0 = 1'b0;
endmodule

module \reg  (
  input  in_1,
  input  in_2,
  input  in_3,
  input  in_4,
  input  in_5,
  output out_6,
  output out_7,
  output out_8,
  output out_9,
  output out_10
);

  wire clock_1_out;

  Clock clock_1 (.out(clock_1_out));
  Register #(.width(1)) register_1 (.D(in_1), .en(1'b1), .Q(out_6), .clk(clock_1_out));  // open: clr
  Register #(.width(1)) register_2 (.D(in_2), .en(1'b1), .Q(out_7), .clk(clock_1_out));  // open: clr
  Register #(.width(1)) register_3 (.D(in_3), .en(1'b1), .Q(out_8), .clk(clock_1_out));  // open: clr
  Register #(.width(1)) register_4 (.D(in_4), .en(1'b1), .Q(out_9), .clk(clock_1_out));  // open: clr
  Register #(.width(1)) register_5 (.D(in_5), .en(1'b1), .Q(out_10), .clk(clock_1_out));  // open: clr
endmodule
