// Logisim project Logisim_mod5_1.circ as structural Verilog: 3 circuits, main circuit mod5
module mod5 (
  input  in_1,
  output out_2,
  output out_3,
  output out_4,
  output out_5,
  output out_6
);

  wire [4:0] reg_1_out_2;

  trans trans_1 (.\input (in_1), .in_2(reg_1_out_2), .out_3({out_6, out_5, out_4, out_3, out_2}));
  \reg  reg_1 (.in_1({out_6, out_5, out_4, out_3, out_2}), .out_2(reg_1_out_2));
endmodule

module trans (
  input  \input ,
  input  [4:0] in_2,
  output [4:0] out_3
);

  wire and_1_out, and_2_out, and_3_out, and_4_out, and_5_out, and_6_out, not_1_out, not_2_out, not_3_out,
       not_4_out, not_5_out, not_6_out, not_7_out;

  not not_1 (not_1_out, \input );
  not not_2 (not_2_out, in_2[2]);
  not not_3 (not_3_out, in_2[2]);
  and and_1 (and_1_out, \input , in_2[3]);
  and and_2 (and_2_out, \input , in_2[2]);
  not not_4 (not_4_out, \input );
  not not_5 (not_5_out, \input );
  and and_3 (and_3_out, not_1_out, not_2_out);
  not not_6 (not_6_out, in_2[3]);
  and and_4 (and_4_out, \input , not_3_out);
  not not_7 (not_7_out, in_2[3]);
  or or_1 (out_3[3], and_1_out, and_2_out);
  and and_5 (and_5_out, not_4_out, in_2[3]);
  and and_6 (and_6_out, not_5_out, in_2[2]);
  and and_7 (out_3[1], and_3_out, not_6_out);
  and and_8 (out_3[2], and_4_out, not_7_out);
  or or_2 (out_3[4], and_5_out, and_6_out);

  assign out_3[0] = 1'b0;
endmodule

module \reg  (
  input  [4:0] in_1,
  output [4:0] out_2
);

  wire clock_1_out;

  Clock clock_1 (.out(clock_1_out));
  Register #(.width(1)) register_1 (.D(in_1[0]), .en(1'b1), .Q(out_2[0]), .clk(clock_1_out));  // open: clr
  Register #(.width(1)) register_2 (.D(in_1[1]), .en(1'b1), .Q(out_2[1]), .clk(clock_1_out));  // open: clr
  Register #(.width(1)) register_3 (.D(in_1[2]), .en(1'b1), .Q(out_2[2]), .clk(clock_1_out));  // open: clr
  Register #(.width(1)) register_4 (.D(in_1[3]), .en(1'b1), .Q(out_2[3]), .clk(clock_1_out));  // open: clr
  Register #(.width(1)) register_5 (.D(in_1[4]), .en(1'b1), .Q(out_2[4]), .clk(clock_1_out));  // open: clr
endmodule
