// Logisim project 复用器.circ as structural Verilog: 1 circuit, main circuit main
module main (
  input  in_1,
  input  \控制端_高开低关 ,
  input  in_3,
  input  in_4,
  input  [3:0] \第0路输入 ,
  input  [3:0] in_6,
  input  [3:0] in_7,
  input  [3:0] in_8,
  input  [3:0] in_9,
  input  [1:0] \选择端 ,
  input  [1:0] \选择端_2 ,
  input  \使能端 ,
  input  \使能端_2 ,
  input  \请求0 ,
  input  \优先编码器 ,
  input  in_16,
  input  \请求6 ,
  input  in_18,
  input  [1:0] in_19,
  input  \使能输入端 ,
  input  \请求0_2 ,
  input  \优先编码器_2 ,
  input  in_23,
  input  \请求6_2 ,
  input  \使能输入端_2 ,
  output out_26,
  output out_27,
  output [3:0] out_28,
  output [3:0] out_29,
  output [3:0] out_30,
  output [3:0] out_31,
  output [3:0] out_32,
  output \使能输出端 ,
  output out_34,
  output [2:0] \编号 ,
  output out_36,
  output out_37,
  output out_38,
  output \是否有请求 ,
  output \使能输出端_作为级连使用 ,
  output [2:0] \编号_2 ,
  output \是否有请求_2 
);

  wire undriven;

  Decoder #(.select(2)) decoder_1 (.out0(out_34), .out1(out_36), .out2(out_37), .out3(out_38), .sel(in_19), .en(in_18));
  xor xor_1 (out_27, in_3, in_4);
  Priority_Encoder priority_encoder_1 (.en_in(undriven));  // open: in0, in1, in2, in3, in4, in5, in6, in7, out, gs, en_out
  assign out_26 = \控制端_高开低关  ? in_1 : 1'bz;  // Controlled_Buffer 三态门
  Multiplexer #(.select(2), .width(4)) multiplexer_1 (
    .in0(\第0路输入 ), .in1(in_6), .in2(in_8), .in3(in_9), .out(out_30), .sel(\选择端 ), .en(\使能端 ));
  Controlled_Inverter \u_三态非门  ();  // open: in, out, en
  Demultiplexer #(.select(2), .width(4)) demultiplexer_1 (
    .out0(out_28), .out1(out_29), .out2(out_31), .out3(out_32), .in(in_7), .sel(\选择端_2 ), .en(\使能端_2 ));
  Priority_Encoder priority_encoder_2 (
    .in0(\请求0_2 ), .in2(\优先编码器_2 ), .in4(in_23), .in6(\请求6_2 ), .out(\编号_2 ), .en_in(\使能输入端_2 ),
    .gs(\是否有请求_2 ), .en_out(\使能输出端_作为级连使用 ));  // open: in1, in3, in5, in7
  Priority_Encoder priority_encoder_3 (
    .in0(\请求0 ), .in2(\优先编码器 ), .in4(in_16), .in6(\请求6 ), .out(\编号 ), .en_in(\使能输入端 ), .gs(\是否有请求 ),
    .en_out(\使能输出端 ));  // open: in1, in3, in5, in7

  // Notes on the sheet:
  //   译码器
  //   选择端的位宽位n,则输入源有2^n个
  //   将nn位的选择端，输出为2^n中的一个1
  //   多路选择器
  //   解复用器
endmodule
