// Logisim project 异或门.circ as structural Verilog: 1 circuit, main circuit main
module main (
  input  x,
  input  [3:0] in_2,
  input  y,
  input  in_4,
  input  in_5,
  input  [5:0] in_6,
  output out_7,
  output [3:0] out_8,
  output out_9
);

  wire and_1_out, and_2_out, not_1_out, not_2_out;
  wire [2:0] xor_2_out;
  wire [3:0] bit_extender_1_out, negator_1_out, shifter_1_out;

  not not_1 (not_1_out, x);
  not not_2 (not_2_out, y);
  // Probe on and_1_out
  and and_1 (and_1_out, not_1_out, y);
  and and_2 (and_2_out, x, not_2_out);
  xor xor_1 (out_9, in_4, in_5);
  // Probe on xor_2_out
  assign xor_2_out = in_6[2:0] ^ in_6[5:3];  // XOR_Gate xor_2, 3 bits wide
  or or_1 (out_7, and_1_out, and_2_out);
  assign bit_extender_1_out = {{2{1'b1}}, 2'b10};  // Bit_Extender bit_extender_1
  // Probe on bit_extender_1_out
  Shifter #(.width(4), .shift("ar")) shifter_1 (.in(in_2), .\dist (2'b10), .out(shifter_1_out));
  Negator #(.width(4)) negator_1 (.in(bit_extender_1_out), .out(negator_1_out));
  // Probe on shifter_1_out
  // Probe on negator_1_out
  assign out_8 = negator_1_out ^ shifter_1_out;  // Odd_Parity odd_parity_1, 4 bits wide
  // Probe on out_8

  // Notes on the sheet:
  //   异或门
endmodule
