// Logisim project fibonacci_1 .circ as structural Verilog: 1 circuit, main circuit main
module main (
  input  [2:0] in_1,
  output [3:0] out_2
);

  wire clock_1_out, comparator_1_eq, comparator_1_gt, comparator_2_eq, counter_1_q, or_1_out;
  wire [2:0] counter_2_q;
  wire [3:0] adder_1_out, bit_extender_1_out, counter_3_q, Fn_1_q, Fn_q, multiplexer_1_out, multiplexer_2_out;

  // Probe on Fn_q
  Register #(.width(4)) Fn (.D(multiplexer_2_out), .Q(Fn_q), .clk(clock_1_out));  // open: en, clr
  Multiplexer #(.width(4)) multiplexer_1 (
    .in0(4'b0001), .in1(adder_1_out), .out(multiplexer_1_out), .sel(counter_1_q));  // open: en
  Counter #(.width(1), .max('h1), .ongoal("stay")) counter_1 (
    .Q(counter_1_q), .clk(clock_1_out));  // open: load, D, count, carry, clr
  Clock clock_1 (.out(clock_1_out));
  // Probe on Fn_1_q
  Register #(.width(4)) Fn_1 (.D(multiplexer_1_out), .Q(Fn_1_q), .clk(clock_1_out));  // open: en, clr
  Counter #(.width(3), .max('h7), .ongoal("stay")) counter_2 (
    .Q(counter_2_q), .clk(clock_1_out));  // open: load, D, count, carry, clr
  Multiplexer #(.width(4)) multiplexer_2 (
    .in0(4'b0000), .in1(Fn_1_q), .out(multiplexer_2_out), .sel(or_1_out));  // open: en
  or or_1 (or_1_out, comparator_1_gt, comparator_1_eq);
  Comparator #(.width(3), .mode("unsigned")) comparator_1 (
    .a(counter_2_q), .b(3'b010), .gt(comparator_1_gt), .eq(comparator_1_eq));  // open: lt
  Adder #(.width(4)) adder_1 (.a(Fn_q), .b(Fn_1_q), .out(adder_1_out));  // open: cin, cout
  // Probe on adder_1_out
  Counter #(.width(4), .max('hf), .ongoal("stay")) counter_3 (
    .Q(counter_3_q), .clk(clock_1_out));  // open: load, D, count, carry, clr
  assign bit_extender_1_out = {{1{1'b0}}, in_1};  // Bit_Extender bit_extender_1
  Register #(.width(4), .trigger("high")) register_1 (
    .D(adder_1_out), .Q(out_2), .clk(comparator_2_eq));  // open: en, clr
  Comparator #(.width(4)) comparator_2 (.a(counter_3_q), .b(bit_extender_1_out), .eq(comparator_2_eq));  // open: gt, lt

  // Other names for the same wires on the sheet: In[2:0] = in_1
endmodule
