// Logisim project 辗转相除法.circ as structural Verilog: 1 circuit, main circuit main
module main (
  input  [7:0] in_1,
  input  [7:0] in_2,
  output [7:0] out_3
);

  wire and_1_out, clock_1_out, comparator_1_lt, comparator_2_eq, comparator_3_gt, counter_1_q, not_1_out;
  wire [7:0] divider_1_rem, multiplexer_2_out, multiplexer_3_out, multiplexer_4_out, register_1_q,
       register_2_q;
  wire [15:0] multiplexer_1_out;

  Multiplexer #(.width(16)) multiplexer_1 (
    .in0({in_2, in_1}), .in1({in_1, in_2}), .out(multiplexer_1_out), .sel(comparator_1_lt));  // open: en
  Comparator #(.mode("unsigned")) comparator_1 (.a(in_1), .b(in_2), .lt(comparator_1_lt));  // open: gt, eq
  Clock clock_1 (.out(clock_1_out));
  // Probe on in_1
  // Probe on in_2
  // Probe on register_2_q
  Multiplexer #(.width(8)) multiplexer_2 (
    .in0(multiplexer_1_out[7:0]), .in1(register_2_q), .out(multiplexer_2_out), .sel(counter_1_q));  // open: en
  Multiplexer #(.width(8)) multiplexer_3 (
    .in0(multiplexer_1_out[15:8]), .in1(divider_1_rem), .out(multiplexer_3_out), .sel(counter_1_q));  // open: en
  Counter #(.width(1), .max('h1), .ongoal("stay")) counter_1 (
    .Q(counter_1_q), .clk(clock_1_out));  // open: load, D, count, carry, clr
  Register register_1 (.D(multiplexer_2_out), .Q(register_1_q), .clk(clock_1_out));  // open: en, clr
  Register register_2 (.D(multiplexer_3_out), .Q(register_2_q), .clk(clock_1_out));  // open: en, clr
  Divider divider_1 (.a(register_1_q), .b(register_2_q), .rem(divider_1_rem));  // open: out, upper
  // Probe on divider_1_rem
  // Probe on register_1_q
  Comparator #(.mode("unsigned")) comparator_2 (
    .a(divider_1_rem), .b({8{1'b0}}), .eq(comparator_2_eq));  // open: gt, lt
  // Probe on multiplexer_4_out
  Multiplexer #(.width(8)) multiplexer_4 (
    .in0({8{1'b0}}), .in1(register_2_q), .out(multiplexer_4_out), .sel(comparator_2_eq));  // open: en
  // Probe on out_3
  Register register_3 (.D(multiplexer_4_out), .Q(out_3), .clk(and_1_out));  // open: en, clr
  and and_1 (and_1_out, comparator_3_gt, not_1_out);
  not not_1 (not_1_out, comparator_3_gt);
  Comparator #(.mode("unsigned")) comparator_3 (
    .a(multiplexer_4_out), .b({8{1'b0}}), .gt(comparator_3_gt));  // open: eq, lt

  // Other names for the same wires on the sheet: B[7:0] = in_2; A[7:0] = in_1
endmodule
