// Logisim project 递归数列电路.circ as structural Verilog: 1 circuit, main circuit main
module main (
  input  [4:0] in_1,
  output [31:0] out_2
);

  wire clock_1_out, comparator_1_gt, comparator_2_gt, comparator_3_gt, comparator_4_eq;
  wire [5:0] bit_extender_1_out, counter_1_q, counter_2_q, counter_3_q, counter_4_q;
  wire [31:0] adder_1_out, and_1_out, Fn_1_q, Fn_2_q, Fn_3_q, multiplexer_1_out, multiplexer_2_out,
       multiplexer_3_out;

  // Probe on multiplexer_1_out
  Counter #(.width(6), .max('h3f), .ongoal("stay")) counter_1 (
    .Q(counter_1_q), .clk(clock_1_out));  // open: load, D, count, carry, clr
  // Probe on multiplexer_3_out
  Register #(.width(32)) Fn_3 (.D(multiplexer_1_out), .Q(Fn_3_q), .clk(clock_1_out));  // open: en, clr
  Comparator #(.width(6), .mode("unsigned")) comparator_1 (
    .a(counter_1_q), .b({6{1'b0}}), .gt(comparator_1_gt));  // open: eq, lt
  Counter #(.width(6), .max('h3f), .ongoal("stay")) counter_2 (
    .Q(counter_2_q), .clk(clock_1_out));  // open: load, D, count, carry, clr
  Comparator #(.width(6), .mode("unsigned")) comparator_2 (
    .a(counter_2_q), .b(6'b000010), .gt(comparator_2_gt));  // open: eq, lt
  // Probe on Fn_3_q
  Register #(.width(32)) Fn_2 (.D(multiplexer_3_out), .Q(Fn_2_q), .clk(clock_1_out));  // open: en, clr
  Clock clock_1 (.out(clock_1_out));
  // Probe on multiplexer_2_out
  Multiplexer #(.width(32)) multiplexer_1 (
    .in0({32{1'b0}}), .in1(Fn_2_q), .out(multiplexer_1_out), .sel(comparator_2_gt));  // open: en
  // Probe on Fn_2_q
  Multiplexer #(.width(32)) multiplexer_2 (
    .in0(32'h1), .in1(adder_1_out), .out(multiplexer_2_out), .sel(comparator_1_gt));  // open: en
  Counter #(.width(6), .max('h3f), .ongoal("stay")) counter_3 (
    .Q(counter_3_q), .clk(clock_1_out));  // open: load, D, count, carry, clr
  Comparator #(.width(6), .mode("unsigned")) comparator_3 (
    .a(counter_3_q), .b(6'b000001), .gt(comparator_3_gt));  // open: eq, lt
  // Probe on Fn_1_q
  assign and_1_out = Fn_3_q & Fn_2_q;  // AND_Gate and_1, 32 bits wide
  Register #(.width(32)) Fn_1 (.D(multiplexer_2_out), .Q(Fn_1_q), .clk(clock_1_out));  // open: en, clr
  Multiplexer #(.width(32)) multiplexer_3 (
    .in0({32{1'b0}}), .in1(Fn_1_q), .out(multiplexer_3_out), .sel(comparator_3_gt));  // open: en
  Adder #(.width(32)) adder_1 (.a(and_1_out), .b(Fn_1_q), .out(adder_1_out));  // open: cin, cout
  // Probe on adder_1_out
  Counter #(.width(6), .max('h3f), .ongoal("stay")) counter_4 (
    .Q(counter_4_q), .clk(clock_1_out));  // open: load, D, count, carry, clr
  // Probe on and_1_out
  Comparator #(.width(6), .mode("unsigned")) comparator_4 (
    .a(counter_4_q), .b(bit_extender_1_out), .eq(comparator_4_eq));  // open: gt, lt
  assign bit_extender_1_out = {{1{1'b0}}, in_1};  // Bit_Extender bit_extender_1
  Register #(.width(32), .trigger("high")) register_1 (
    .D(adder_1_out), .Q(out_2), .clk(comparator_4_eq));  // open: en, clr

  // Other names for the same wires on the sheet: In[4:0] = in_1
endmodule
