// Logisim project CPU_right.circ as structural Verilog: 8 circuits, main circuit main
module main (
  input  Reset,
  output [31:0] out_2,
  output out_3,
  output [4:0] out_4,
  output [31:0] out_5,
  output out_6,
  output [4:0] out_7,
  output [31:0] out_8
);

  wire clk, comparator_1_eq, Equal, EXTop, Less, Zero;
  wire [1:0] ALUsrc, DMop, MemtoReg, NPCop, RegDst;
  wire [2:0] ALUctrl, BranchOp;
  wire [31:0] adder_1_out, dm_1_rd, ext_1_extimm, grf_1_rd1, MemAddr, multiplexer_2_out, multiplexer_3_out,
       PC, s;

  Clock clock_1 (.out(clk));
  IFU ifu_1 (
    .Instr(out_2), .NPCop(NPCop), .instr_index(out_2[25:0]), .offset(out_2[15:0]), .Reg(grf_1_rd1),
    .in_1(clk), .in_2(Reset), .PC(PC), .Branchop(BranchOp), .Equal(Equal), .Less(Less));
  // Probe on grf_1_rd1
  assign s = {{27{1'b0}}, out_2[10:6]};  // Bit_Extender bit_extender_1
  Multiplexer #(.select(2), .width(5), .enable("false")) multiplexer_1 (
    .in0(out_2[20:16]), .in1(out_2[15:11]), .in2({5{1'b1}}), .out(out_4), .sel(RegDst));  // open: in3
  CTRL ctrl_1 (
    .Op(out_2[31:26]), .Func(out_2[5:0]), .RegDst(RegDst), .RegWrite(out_3), .EXTop(EXTop), .ALUsrc(ALUsrc),
    .ALUctrl(ALUctrl), .Memwrite(out_6), .MemtoReg(MemtoReg), .NPCop(NPCop), .Branchop(BranchOp),
    .DMop(DMop), .in_1(Zero));
  GRF grf_1 (
    .A1(out_2[25:21]), .A2(out_2[20:16]), .A3(out_4), .WD(out_5), .RD1(grf_1_rd1), .RD2(out_8), .clk(clk),
    .reset(Reset), .WE(out_3));
  EXT ext_1 (.Extop(EXTop), .Imm(out_2[15:0]), .ExtImm(ext_1_extimm));
  Comparator #(.width(2), .mode("unsigned")) comparator_1 (
    .a(2'b10), .b(ALUsrc), .eq(comparator_1_eq));  // open: gt, lt
  Multiplexer #(.width(32), .enable("false")) multiplexer_2 (
    .in0(grf_1_rd1), .in1(out_8), .out(multiplexer_2_out), .sel(comparator_1_eq));
  Multiplexer #(.select(2), .width(32), .enable("false")) multiplexer_3 (
    .in0(out_8), .in1(ext_1_extimm), .in2(s), .out(multiplexer_3_out), .sel(ALUsrc));  // open: in3
  // Probe on s
  ALU alu_1 (
    .SrcA(multiplexer_2_out), .SrcB(multiplexer_3_out), .Equal(Equal),
    .ALUResult({MemAddr[31:7], out_7, MemAddr[1:0]}), .ALUctrl(ALUctrl), .Less(Less), .Zero(Zero));
  // Probe on ALUsrc
  // Probe on ALUctrl
  DM dm_1 (
    .WD(out_8), .RD(dm_1_rd), .clk(clk), .in_2(Reset), .in_3(out_6),
    .A({MemAddr[31:7], out_7, MemAddr[1:0]}), .DMop(DMop));
  Adder #(.width(32)) adder_1 (.a(PC), .b(32'h4), .out(adder_1_out));  // open: cin, cout
  Multiplexer #(.select(2), .width(32), .enable("false")) multiplexer_4 (
    .in0({MemAddr[31:7], out_7, MemAddr[1:0]}), .in1(dm_1_rd), .in2(adder_1_out),
    .in3({MemAddr[15:7], out_7, MemAddr[1:0], {16{1'b0}}}), .out(out_5), .sel(MemtoReg));
  // Probe on MemtoReg

  // Other names for the same wires on the sheet: MemAddr[6:2] = out_7; Instr[31:0] = out_2; MemData[31:0] = out_8;
  //   Memwrite = out_6; RegAddr[4:0] = out_4; RegData[31:0] = out_5; RegWrite = out_3
endmodule

module IFU (
  input  in_1,
  input  in_2,
  input  [1:0] NPCop,
  input  [25:0] instr_index,
  input  [15:0] offset,
  input  [2:0] Branchop,
  input  [31:0] Reg,
  input  Less,
  input  Equal,
  output [31:0] PC,
  output [31:0] Instr
);

  wire and_1_out, not_1_out, not_2_out, not_3_out, or_1_out;
  wire [31:0] npc_1_npc;

  Register #(.width(32)) register_1 (.D(npc_1_npc), .Q(PC), .clk(in_1), .clr(in_2));  // open: en
  NPC npc_1 (
    .PC(PC), .NPCop(NPCop), .instr_index(instr_index), .offset(offset), .Reg(Reg), .NPC(npc_1_npc),
    .equal(Equal), .n_equal(not_2_out), .less(Less), .big(and_1_out), .less_or_equal(or_1_out),
    .big_or_equal(not_3_out), .Branchop(Branchop));
  or or_1 (or_1_out, Less, Equal);
  and and_1 (and_1_out, not_3_out, not_1_out);
  not not_1 (not_1_out, Equal);
  not not_2 (not_2_out, Equal);
  not not_3 (not_3_out, Less);
  // Probe on nothing
  ROM #(.addrWidth(5), .dataWidth(32)) rom_1 (.addr(PC[6:2]), .data(Instr));  // open: sel

  // Other names for the same wires on the sheet: clk = in_1; Reset = in_2

  // Notes on the sheet:
  //   contents of rom_1 (hex, n*v repeats v):
  //   34040123 341f3018 3e40031 34050789 3c060123 34100123 34110456
endmodule

module NPC (
  input  [31:0] PC,
  input  [1:0] NPCop,
  input  equal,
  input  [25:0] instr_index,
  input  n_equal,
  input  less,
  input  big,
  input  [15:0] offset,
  input  less_or_equal,
  input  big_or_equal,
  input  [31:0] Reg,
  input  [2:0] Branchop,
  output [31:0] NPC
);

  wire multiplexer_2_out;
  wire [31:0] adder_2_out, adder_3_out, bit_extender_1_out, O1, O3;

  Adder #(.width(32)) adder_1 (.a(PC), .b(32'h4), .out(O1));  // open: cin, cout
  Adder #(.width(32)) adder_2 (.a(PC), .b(32'h4), .out(adder_2_out));  // open: cin, cout
  Adder #(.width(32)) adder_3 (.a(adder_2_out), .b(bit_extender_1_out), .out(adder_3_out));  // open: cin, cout
  assign bit_extender_1_out = {{14{offset[15]}}, {offset, 2'b00}};  // Bit_Extender bit_extender_1
  Multiplexer #(.width(32), .enable("false")) multiplexer_1 (
    .in0(adder_2_out), .in1(adder_3_out), .out(O3), .sel(multiplexer_2_out));
  Multiplexer #(.select(3), .enable("false")) multiplexer_2 (
    .in0(equal), .in1(n_equal), .in2(less), .in3(big), .in4(less_or_equal), .in5(big_or_equal),
    .out(multiplexer_2_out), .sel(Branchop));  // open: in6, in7
  Multiplexer #(.select(2), .width(32), .enable("false")) multiplexer_3 (
    .in0(O1), .in1({PC[31:28], instr_index, 2'b00}), .in2(O3), .in3(Reg), .out(NPC), .sel(NPCop));

  // Other names for the same wires on the sheet: O2[31:2] = {PC[31:28], instr_index}; O4[31:0] = Reg
endmodule

module GRF (
  input  clk,
  input  reset,
  input  WE,
  input  [4:0] A1,
  input  [4:0] A2,
  input  [4:0] A3,
  input  [31:0] WD,
  output [31:0] RD1,
  output [31:0] RD2
);

  wire e0, e1, e2, e3, e4, e5, e6, e7, e8, e9, e10, e11, e12, e13, e14, e15, e16, e17, e18, e19, e20, e21,
       e22, e23, e24, e25, e26, e27, e28, e29, e30, e31;
  wire [31:0] I0, I1, I2, I3, I4, I5, I6, I7, I8, I9, I10, I11, I12, I13, I14, I15, I16, I17, I18, I19, I20,
       I21, I22, I23, I24, I25, I26, I27, I28, I29, I30, I31, O0, O1, O2, O3, O4, O5, O6, O7, O8, O9, O10,
       O11, O12, O13, O14, O15, O16, O17, O18, O19, O20, O21, O22, O23, O24, O25, O26, O27, O28, O29, O30,
       O31;

  Register #(.width(32)) register_1 (.D(I0), .en(e0), .Q(O0), .clk(clk), .clr(reset));
  Register #(.width(32)) register_2 (.D(I4), .en(e4), .Q(O4), .clk(clk), .clr(reset));
  Register #(.width(32)) register_3 (.D(I8), .en(e8), .Q(O8), .clk(clk), .clr(reset));
  Register #(.width(32)) register_4 (.D(I12), .en(e12), .Q(O12), .clk(clk), .clr(reset));
  Register #(.width(32)) register_5 (.D(I16), .en(e16), .Q(O16), .clk(clk), .clr(reset));
  Register #(.width(32)) register_6 (.D(I20), .en(e20), .Q(O20), .clk(clk), .clr(reset));
  Register #(.width(32)) register_7 (.D(I24), .en(e24), .Q(O24), .clk(clk), .clr(reset));
  Register #(.width(32)) register_8 (.D(I28), .en(e28), .Q(O28), .clk(clk), .clr(reset));
  Demultiplexer #(.select(5), .width(32)) demultiplexer_1 (
    .out0(I0), .out1(I1), .out2(I2), .out3(I3), .out4(I4), .out5(I5), .out6(I6), .out7(I7), .out8(I8),
    .out9(I9), .out10(I10), .out11(I11), .out12(I12), .out13(I13), .out14(I14), .out15(I15), .out16(I16),
    .out17(I17), .out18(I18), .out19(I19), .out20(I20), .out21(I21), .out22(I22), .out23(I23), .out24(I24),
    .out25(I25), .out26(I26), .out27(I27), .out28(I28), .out29(I29), .out30(I30), .out31(I31), .in(WD),
    .sel(A3));  // open: en
  Register #(.width(32)) register_9 (.D(I1), .en(e1), .Q(O1), .clk(clk), .clr(reset));
  Register #(.width(32)) register_10 (.D(I5), .en(e5), .Q(O5), .clk(clk), .clr(reset));
  Register #(.width(32)) register_11 (.D(I9), .en(e9), .Q(O9), .clk(clk), .clr(reset));
  Register #(.width(32)) register_12 (.D(I13), .en(e13), .Q(O13), .clk(clk), .clr(reset));
  Register #(.width(32)) register_13 (.D(I17), .en(e17), .Q(O17), .clk(clk), .clr(reset));
  Register #(.width(32)) register_14 (.D(I21), .en(e21), .Q(O21), .clk(clk), .clr(reset));
  Register #(.width(32)) register_15 (.D(I25), .en(e25), .Q(O25), .clk(clk), .clr(reset));
  Register #(.width(32)) register_16 (.D(I29), .en(e29), .Q(O29), .clk(clk), .clr(reset));
  Register #(.width(32)) register_17 (.D(I2), .en(e2), .Q(O2), .clk(clk), .clr(reset));
  Register #(.width(32)) register_18 (.D(I6), .en(e6), .Q(O6), .clk(clk), .clr(reset));
  Register #(.width(32)) register_19 (.D(I10), .en(e10), .Q(O10), .clk(clk), .clr(reset));
  Register #(.width(32)) register_20 (.D(I14), .en(e14), .Q(O14), .clk(clk), .clr(reset));
  Register #(.width(32)) register_21 (.D(I18), .en(e18), .Q(O18), .clk(clk), .clr(reset));
  Register #(.width(32)) register_22 (.D(I22), .en(e22), .Q(O22), .clk(clk), .clr(reset));
  Register #(.width(32)) register_23 (.D(I26), .en(e26), .Q(O26), .clk(clk), .clr(reset));
  Register #(.width(32)) register_24 (.D(I30), .en(e30), .Q(O30), .clk(clk), .clr(reset));
  Register #(.width(32)) register_25 (.D(I3), .en(e3), .Q(O3), .clk(clk), .clr(reset));
  Register #(.width(32)) register_26 (.D(I7), .en(e7), .Q(O7), .clk(clk), .clr(reset));
  Register #(.width(32)) register_27 (.D(I11), .en(e11), .Q(O11), .clk(clk), .clr(reset));
  Register #(.width(32)) register_28 (.D(I15), .en(e15), .Q(O15), .clk(clk), .clr(reset));
  Register #(.width(32)) register_29 (.D(I19), .en(e19), .Q(O19), .clk(clk), .clr(reset));
  Register #(.width(32)) register_30 (.D(I23), .en(e23), .Q(O23), .clk(clk), .clr(reset));
  Register #(.width(32)) register_31 (.D(I27), .en(e27), .Q(O27), .clk(clk), .clr(reset));
  Register #(.width(32)) register_32 (.D(I31), .en(e31), .Q(O31), .clk(clk), .clr(reset));
  Demultiplexer #(.select(5), .disabled(0)) demultiplexer_2 (
    .out0(e0), .out1(e1), .out2(e2), .out3(e3), .out4(e4), .out5(e5), .out6(e6), .out7(e7), .out8(e8),
    .out9(e9), .out10(e10), .out11(e11), .out12(e12), .out13(e13), .out14(e14), .out15(e15), .out16(e16),
    .out17(e17), .out18(e18), .out19(e19), .out20(e20), .out21(e21), .out22(e22), .out23(e23), .out24(e24),
    .out25(e25), .out26(e26), .out27(e27), .out28(e28), .out29(e29), .out30(e30), .out31(e31), .in(1'b1),
    .sel(A3), .en(WE));
  Multiplexer #(.select(5), .width(32)) multiplexer_1 (
    .in0({32{1'b0}}), .in1(O1), .in2(O2), .in3(O3), .in4(O4), .in5(O5), .in6(O6), .in7(O7), .in8(O8),
    .in9(O9), .in10(O10), .in11(O11), .in12(O12), .in13(O13), .in14(O14), .in15(O15), .in16(O16), .in17(O17),
    .in18(O18), .in19(O19), .in20(O20), .in21(O21), .in22(O22), .in23(O23), .in24(O24), .in25(O25),
    .in26(O26), .in27(O27), .in28(O28), .in29(O29), .in30(O30), .in31(O31), .out(RD1), .sel(A1));  // open: en
  Multiplexer #(.select(5), .width(32)) multiplexer_2 (
    .in0({32{1'b0}}), .in1(O1), .in2(O2), .in3(O3), .in4(O4), .in5(O5), .in6(O6), .in7(O7), .in8(O8),
    .in9(O9), .in10(O10), .in11(O11), .in12(O12), .in13(O13), .in14(O14), .in15(O15), .in16(O16), .in17(O17),
    .in18(O18), .in19(O19), .in20(O20), .in21(O21), .in22(O22), .in23(O23), .in24(O24), .in25(O25),
    .in26(O26), .in27(O27), .in28(O28), .in29(O29), .in30(O30), .in31(O31), .out(RD2), .sel(A2));  // open: en

  // Other names for the same wires on the sheet: enslt = WE
endmodule

module ALU (
  input  [2:0] ALUctrl,
  input  [31:0] SrcA,
  input  [31:0] SrcB,
  output Equal,
  output Less,
  output [31:0] ALUResult,
  output Zero
);

  wire comparator_1_lt, comparator_4_eq, comparator_5_eq;
  wire [31:0] adder_1_out, and_1_out, bit_extender_1_out, or_1_out, shifter_1_out, shifter_2_out,
       shifter_3_out, subtractor_1_out;

  assign or_1_out = SrcA | SrcB;  // OR_Gate or_1, 32 bits wide
  assign and_1_out = SrcA & SrcB;  // AND_Gate and_1, 32 bits wide
  Comparator #(.width(32)) comparator_1 (.a(SrcA), .b(SrcB), .lt(comparator_1_lt));  // open: gt, eq
  Adder #(.width(32)) adder_1 (.a(SrcA), .b(SrcB), .out(adder_1_out));  // open: cin, cout
  Subtractor #(.width(32)) subtractor_1 (.a(SrcA), .b(SrcB), .out(subtractor_1_out));  // open: bin, bout
  Shifter #(.width(32), .shift("lr")) shifter_1 (.in(SrcA), .\dist (SrcB[4:0]), .out(shifter_1_out));
  Shifter #(.width(32), .shift("ar")) shifter_2 (.in(SrcA), .\dist (SrcB[4:0]), .out(shifter_2_out));
  assign bit_extender_1_out = {{31{1'b0}}, comparator_1_lt};  // Bit_Extender bit_extender_1
  Shifter #(.width(32)) shifter_3 (.in(SrcA), .\dist (SrcB[4:0]), .out(shifter_3_out));
  Multiplexer #(.select(3), .width(32), .enable("false")) multiplexer_1 (
    .in0(adder_1_out), .in1(subtractor_1_out), .in2(or_1_out), .in3(and_1_out), .in4(shifter_1_out),
    .in5(shifter_2_out), .in6(bit_extender_1_out), .in7(shifter_3_out), .out(ALUResult), .sel(ALUctrl));
  Comparator #(.width(32)) comparator_2 (.a(SrcA), .b(SrcB), .eq(Equal));  // open: gt, lt
  Comparator #(.width(32)) comparator_3 (.a(SrcA), .b(SrcB), .lt(Less));  // open: gt, eq
  // Probe on ALUResult
  Comparator #(.width(32), .mode("unsigned")) comparator_4 (
    .a(SrcB), .b({32{1'b0}}), .eq(comparator_4_eq));  // open: gt, lt
  Comparator #(.width(3), .mode("unsigned")) comparator_5 (
    .a(ALUctrl), .b(3'b101), .eq(comparator_5_eq));  // open: gt, lt
  Multiplexer #(.enable("false")) multiplexer_2 (.in0(1'b1), .in1(comparator_4_eq), .out(Zero), .sel(comparator_5_eq));

  // Other names for the same wires on the sheet: A[31:0] = SrcA; B[31:0] = SrcB; Operation[2:0] = ALUctrl
endmodule

module DM (
  input  clk,
  input  in_2,
  input  in_3,
  input  [1:0] DMop,
  input  [31:0] A,
  input  [31:0] WD,
  output [31:0] RD
);

  wire [7:0] multiplexer_5_out, RD_0_7, RD_8_15, RD_16_23, RD_24_31;
  wire [15:0] multiplexer_4_out;
  wire [31:0] bit_extender_1_out, bit_extender_2_out, Data, multiplexer_1_out, multiplexer_2_out;

  Multiplexer #(.width(32), .enable("false")) multiplexer_1 (
    .in0({RD_24_31, RD_16_23, WD[15:0]}), .in1({WD[15:0], RD_8_15, RD_0_7}), .out(multiplexer_1_out),
    .sel(A[1]));
  Multiplexer #(.select(2), .width(32), .enable("false")) multiplexer_2 (
    .in0({RD_24_31, RD_16_23, RD_8_15, WD[7:0]}), .in1({RD_24_31, RD_16_23, WD[7:0], RD_0_7}),
    .in2({RD_24_31, WD[7:0], RD_8_15, RD_0_7}), .in3({WD[7:0], RD_16_23, RD_8_15, RD_0_7}),
    .out(multiplexer_2_out), .sel(A[1:0]));
  Multiplexer #(.select(2), .width(32), .enable("false")) multiplexer_3 (
    .in0(WD), .in1(multiplexer_1_out), .in2(multiplexer_2_out), .out(Data), .sel(DMop));  // open: in3
  RAM #(.addrWidth(5), .dataWidth(32), .bus("separate")) ram_1 (
    .addr(A[6:2]), .din(Data), .data({RD_24_31, RD_16_23, RD_8_15, RD_0_7}), .str(in_3), .clk(clk), .clr(in_2));  // open: sel, ld
  Multiplexer #(.width(16), .enable("false")) multiplexer_4 (
    .in0({RD_8_15, RD_0_7}), .in1({RD_24_31, RD_16_23}), .out(multiplexer_4_out), .sel(A[1]));
  Multiplexer #(.select(2), .width(8), .enable("false")) multiplexer_5 (
    .in0(RD_0_7), .in1(RD_8_15), .in2(RD_16_23), .in3(RD_24_31), .out(multiplexer_5_out), .sel(A[1:0]));
  assign bit_extender_1_out = {{16{multiplexer_4_out[15]}}, multiplexer_4_out};  // Bit_Extender bit_extender_1
  assign bit_extender_2_out = {{24{multiplexer_5_out[7]}}, multiplexer_5_out};  // Bit_Extender bit_extender_2
  Multiplexer #(.select(2), .width(32), .enable("false")) multiplexer_6 (
    .in0({RD_24_31, RD_16_23, RD_8_15, RD_0_7}), .in1(bit_extender_1_out), .in2(bit_extender_2_out),
    .out(RD), .sel(DMop));  // open: in3

  // Other names for the same wires on the sheet: WD_0_7[7:0] = WD[7:0]; WD_8_15[7:0] = WD[15:8];
  //   WD_16_23[7:0] = WD[23:16]; WD_24_31[7:0] = WD[31:24]; Add[31:0] = A; Reset = in_2; WE = in_3
endmodule

module EXT (
  input  Extop,
  input  [15:0] Imm,
  output [31:0] ExtImm
);

  wire [31:0] bit_extender_1_out, bit_extender_2_out;

  assign bit_extender_1_out = {{16{1'b0}}, Imm};  // Bit_Extender bit_extender_1
  assign bit_extender_2_out = {{16{Imm[15]}}, Imm};  // Bit_Extender bit_extender_2
  Multiplexer #(.width(32), .enable("false")) multiplexer_1 (
    .in0(bit_extender_1_out), .in1(bit_extender_2_out), .out(ExtImm), .sel(Extop));
endmodule

module CTRL (
  input  in_1,
  input  [5:0] Op,
  input  [5:0] Func,
  output [1:0] NPCop,
  output RegWrite,
  output [1:0] RegDst,
  output EXTop,
  output [1:0] ALUsrc,
  output [2:0] ALUctrl,
  output Memwrite,
  output [1:0] MemtoReg,
  output [2:0] Branchop,
  output [1:0] DMop
);

  wire add_out, beq_out, bezal_out, lb_out, lh_out, lui_out, lw_out, not_1_out, not_2_out, not_3_out,
       not_4_out, not_5_out, not_6_out, not_7_out, not_8_out, not_9_out, not_10_out, not_11_out, not_12_out,
       ori_out, R_out, RegWrite_out, sb_out, sh_out, sll_out, sub_out, sw_out;
  wire [1:0] NPCop_0_out;

  not not_1 (not_1_out, Op[5]);
  not not_2 (not_2_out, Op[4]);
  not not_3 (not_3_out, Op[3]);
  not not_4 (not_4_out, Op[1]);
  not not_5 (not_5_out, Op[2]);
  not not_6 (not_6_out, Op[0]);
  and R (R_out, not_1_out, not_2_out, not_3_out, not_5_out, not_4_out, not_6_out);
  not not_7 (not_7_out, Func[5]);
  not not_8 (not_8_out, Func[4]);
  not not_9 (not_9_out, Func[2]);
  not not_10 (not_10_out, Func[3]);
  not not_11 (not_11_out, Func[1]);
  not not_12 (not_12_out, Func[0]);
  and add (add_out, Func[5], not_8_out, not_10_out, not_9_out, not_11_out, not_12_out, R_out);
  and sub (sub_out, Func[5], not_8_out, not_10_out, not_9_out, Func[1], not_12_out, R_out);
  and ori (ori_out, not_1_out, not_2_out, Op[3], Op[2], not_4_out, Op[0]);
  and lw (lw_out, Op[5], not_2_out, not_3_out, not_5_out, Op[1], Op[0]);
  and sw (sw_out, Op[5], not_2_out, Op[3], not_5_out, Op[1], Op[0]);
  and beq (beq_out, not_1_out, not_2_out, not_3_out, Op[2], not_4_out, not_6_out);
  and lui (lui_out, not_1_out, not_2_out, Op[3], Op[2], Op[1], Op[0]);
  and sll (sll_out, R_out, not_7_out, not_8_out, not_10_out, not_9_out, not_11_out, not_12_out);
  and lh (lh_out, Op[5], not_2_out, not_3_out, not_5_out, not_4_out, Op[0]);
  and sh (sh_out, Op[5], not_2_out, Op[3], not_5_out, not_4_out, Op[0]);
  and lb (lb_out, Op[5], not_2_out, not_3_out, not_5_out, not_4_out, not_6_out);
  and sb (sb_out, Op[5], not_2_out, Op[3], not_5_out, not_4_out, not_6_out);
  and bezal (bezal_out, R_out, Func[5], Func[4], not_10_out, not_9_out, not_11_out, Func[0]);
  or RegDst_1 (RegDst[1], 1'b0, bezal_out);
  or RegDst_0 (RegDst[0], 1'b0, add_out, sub_out, sll_out);
  Multiplexer #(.enable("false")) multiplexer_1 (.in0(1'b0), .in1(RegWrite_out), .out(RegWrite), .sel(in_1));
  or u_RegWrite (RegWrite_out, 1'b0, add_out, sub_out, ori_out, lw_out, lui_out, sll_out, lh_out, lb_out, bezal_out);
  or u_EXTop (EXTop, 1'b0, lw_out, sw_out, lh_out, sh_out, lb_out, sb_out);
  or ALUsrc_1 (ALUsrc[1], 1'b0, sll_out);
  or ALUsrc_0 (ALUsrc[0], 1'b0, ori_out, lw_out, sw_out, lui_out, lh_out, sh_out, lb_out, sb_out);
  or ALUctrl_2 (ALUctrl[2], 1'b0, sll_out, bezal_out);
  or ALUctrl_1 (ALUctrl[1], 1'b0, ori_out, sll_out);
  or ALUctrl_0 (ALUctrl[0], 1'b0, sub_out, sll_out, bezal_out);
  or u_Memwrite (Memwrite, 1'b0, sw_out, sh_out, sb_out);
  or MemtoReg_1 (MemtoReg[1], 1'b0, lui_out, bezal_out);
  or MemtoReg_0 (MemtoReg[0], 1'b0, lw_out, lui_out, lh_out, lb_out);
  Multiplexer #(.width(2), .enable("false")) multiplexer_2 (.in0(2'b00), .in1(NPCop_0_out), .out(NPCop), .sel(in_1));
  or NPCop_1 (NPCop_0_out[1], 1'b0, beq_out, bezal_out);
  or NPCop_0 (NPCop_0_out[0], 1'b0, bezal_out);
  buf Branchop_2 (Branchop[2], 1'b0);  // OR_Gate
  buf Branchop_1 (Branchop[1], 1'b0);  // OR_Gate
  buf Branchop_0 (Branchop[0], 1'b0);  // OR_Gate
  or DMop_1 (DMop[1], 1'b0, lb_out, sb_out);
  or DMop_0 (DMop[0], 1'b0, lh_out, sh_out);

  // Other names for the same wires on the sheet: Zero = in_1
endmodule
